# Fritzing sketch PiPicoJamma1.2 (saved by Fritzing 0.9.9b)
circuit board: 11.6cm x 7.43946cm
circuit board: 3.41488cm x 5.05211cm
breadboards: 1

parts:
  J1 = Jamma Finger [package=THT]
  Red2 = Resistor [tolerance=±5% power=0.25 resistance=8.2k package=THT]
  Red3 = Resistor [tolerance=±5% power=0.25 resistance=4.3k package=THT]
  Red4 = Resistor [tolerance=±5% power=0.25 resistance=2.2k package=THT]
  Red5 = Resistor [tolerance=±5% power=0.25 resistance=1k package=THT]
  Red6 = Resistor [tolerance=±5% power=0.25 resistance=510 package=THT]
  Red7 = Resistor [tolerance=±5% power=0.25 resistance=180 package=THT]
  Blue2 = Resistor [tolerance=±5% power=0.25 resistance=8.2k package=THT]
  Blue5 = Resistor [tolerance=±5% power=0.25 resistance=1k package=THT]
  Blue7 = Resistor [tolerance=±5% power=0.25 resistance=180 package=THT]
  Blue6 = Resistor [tolerance=±5% power=0.25 resistance=510 package=THT]
  Blue3 = Resistor [tolerance=±5% power=0.25 resistance=4.3k package=THT]
  Blue4 = Resistor [tolerance=±5% power=0.25 resistance=2.2k package=THT]
  Green7 = Resistor [tolerance=±5% power=0.25 resistance=180 package=THT]
  Green4 = Resistor [tolerance=±5% power=0.25 resistance=2.2k package=THT]
  Green2 = Resistor [tolerance=±5% power=0.25 resistance=8.2k package=THT]
  Green5 = Resistor [tolerance=±5% power=0.25 resistance=1k package=THT]
  Green6 = Resistor [tolerance=±5% power=0.25 resistance=510 package=THT]
  Green3 = Resistor [tolerance=±5% power=0.25 resistance=4.3k package=THT]
  Raspberry_Pi_3/4 = Raspberry Pi 4 [part_number=RPI-4-b]
  J2 = female pin header, 10 pins [form="♀ (female)"]
  Raspberry_Pi_Pico = Raspberry Pi Pico
  TRS1 = Audio Jack (TRS) 3.5mm [package="4Ucon 08780 [THT]"]
  SW1 = male pin header, 2 pins [form="♂ (male)"]  # not connected
  +12v_GND1 = male pin header, 2 pins [form="♂ (male)"]
  L-_L+1 = male pin header, 2 pins [form="♂ (male)"]
  RIn_G_LIn1 = male pin header, 3 pins [form="♂ (male)"]
  R-_R+1 = male pin header, 2 pins [form="♂ (male)"]
  J3 = female pin header, 2 pins [form="♀ (female)"]
  Volume = Stereo POT [package=THT]
  R+_R- = Terminal 2pin
  L+_L- = Terminal 2pin
  J4 = female pin header, 1 pin [form="♀ (female)"]
  J5 = female pin header, 1 pin [form="♀ (female)"]
  J6 = female pin header, 3 pins [form="♀ (female)"]
  J11 = female pin header, 2 pins [form="♀ (female)"]
  J12 = female pin header, 2 pins [form="♀ (female)"]
  +5V_GND = female pin header, 2 pins [form="♀ (female)"]
  Audio_R = Pad [width=1.8 height=1.8 connect=center]
  Audio_L = Pad [width=1.8 height=1.8 connect=center]
  J13 = female pin header, 2 pins [form="♀ (female)"]
  J14 = female pin header, 2 pins [form="♀ (female)"]
  J15 = female pin header, 6 pins [form="♀ (female)"]
  J16 = female pin header, 6 pins [form="♀ (female)"]
  J24 = female pin header, 2 pins [form="♀ (female)"]
  J25 = female pin header, 2 pins [form="♀ (female)"]
  J26 = female pin header, 5 pins [form="♀ (female)"]
  Arduino_Pro_Micro = Arduino Pro Micro (Clone)
  Logic_Conv = Logic Level Converter
  74F04_PWR = 74LS04 [package="DIP (Dual Inline) [THT]"]  # not connected
  74F04 = 74LS04 [chip_label=IC package="DIP (Dual Inline) [THT]"]
  74F04_E = 74LS04 [package="DIP (Dual Inline) [THT]"]  # not connected
  74F04_A = 74LS04 [package="DIP (Dual Inline) [THT]"]  # not connected
  74F04_D = 74LS04 [package="DIP (Dual Inline) [THT]"]  # not connected
  74F04_F = 74LS04 [package="DIP (Dual Inline) [THT]"]  # not connected
  74F04_B = 74LS04 [package="DIP (Dual Inline) [THT]"]  # not connected
  74F04_C = 74LS04 [package="DIP (Dual Inline) [THT]"]  # not connected

nets:
  N1: J1.pin1, J1.pin2, J1.pin14, +12v_GND1.pin1, +5V_GND.pin1
  N2: J1.pin3, J1.pin4, +5V_GND.pin2
  N3: J1.pin6, +12v_GND1.pin2
  N4: J1.pin10, R-_R+1.pin2, R+_R-.pin_1
  N5: J1.pin12, Red2.Pin_1, Red3.Pin_1, Red4.Pin_1, Red5.Pin_1, Red6.Pin_1, Red7.Pin_1
  N6: J1.pin13, Blue2.Pin_1, Blue5.Pin_1, Blue7.Pin_1, Blue6.Pin_1, Blue3.Pin_1, Blue4.Pin_1
  N7: J1.pin15, Raspberry_Pi_Pico.pin_2
  N8: J1.pin16, Raspberry_Pi_Pico.pin_5
  N9: J1.pin17, Raspberry_Pi_Pico.pin_7
  N10: J1.pin18, Raspberry_Pi_Pico.pin_10
  N11: J1.pin19, Raspberry_Pi_Pico.pin_12
  N12: J1.pin20, Raspberry_Pi_Pico.pin_15
  N13: J1.pin21, Raspberry_Pi_Pico.pin_17
  N14: J1.pin22, Raspberry_Pi_Pico.pin_20
  N15: J1.pin23, Raspberry_Pi_Pico.pin_32
  N16: J1.pin24, Raspberry_Pi_Pico.pin_29
  N17: J1.pin25, J2.pin8, Raspberry_Pi_Pico.pin_27
  N18: J1.pin26, J2.pin7, Raspberry_Pi_Pico.pin_26
  N19: J1.pin27, J2.pin6, Raspberry_Pi_Pico.pin_25
  N20: J1.pin30, J2.pin2, Raspberry_Pi_Pico.pin_21
  N21: J1.pin31, J2.pin3, Raspberry_Pi_Pico.pin_22
  N22: J1.pin32, J2.pin4, Raspberry_Pi_Pico.pin_24
  N23: J1.pin33, Raspberry_Pi_Pico.pin_31
  N24: J1.pin34, Raspberry_Pi_Pico.pin_34
  N25: J1.pin35, Raspberry_Pi_Pico.pin_19
  N26: J1.pin36, Raspberry_Pi_Pico.pin_16
  N27: J1.pin37, Raspberry_Pi_Pico.pin_14
  N28: J1.pin38, Raspberry_Pi_Pico.pin_11
  N29: J1.pin39, Raspberry_Pi_Pico.pin_9
  N30: J1.pin40, Raspberry_Pi_Pico.pin_6
  N31: J1.pin41, Raspberry_Pi_Pico.pin_4
  N32: J1.pin43, Raspberry_Pi_Pico.pin_1
  N33: J1.pin44, J13.pin1, J14.pin1
  N34: J1.pin45, Green7.Pin_1, Green4.Pin_1, Green2.Pin_1, Green5.Pin_1, Green6.Pin_1, Green3.Pin_1
  N35: J1.pin47, R-_R+1.pin1, R+_R-.pin_2
  N36: J1.pin53, J1.pin54
  N37: J1.pin55, J1.pin56, Raspberry_Pi_3/4.GND, Raspberry_Pi_Pico.pin_3, Raspberry_Pi_Pico.pin_23, Raspberry_Pi_Pico.pin_33, Raspberry_Pi_Pico.pin_38, Raspberry_Pi_Pico.pin_42, J3.pin2, J11.pin2, J12.pin2, J15.pin3
  N38: Red2.Pin_0, Raspberry_Pi_3/4.GPIO16
  N39: Red3.Pin_0, Raspberry_Pi_3/4.GPIO17
  N40: Red4.Pin_0, Raspberry_Pi_3/4.GPIO18
  N41: Red5.Pin_0, Raspberry_Pi_3/4.GPIO19
  N42: Red6.Pin_0, Raspberry_Pi_3/4.GPIO20
  N43: Red7.Pin_0, Raspberry_Pi_3/4.GPIO21
  N44: Blue2.Pin_0, Raspberry_Pi_3/4.GPIO4
  N45: Blue5.Pin_0, Raspberry_Pi_3/4.GPIO7
  N46: Blue7.Pin_0, Raspberry_Pi_3/4.GPIO9
  N47: Blue6.Pin_0, Raspberry_Pi_3/4.GPIO8
  N48: Blue3.Pin_0, Raspberry_Pi_3/4.GPIO5
  N49: Blue4.Pin_0, Raspberry_Pi_3/4.GPIO6
  N50: Green7.Pin_0, Raspberry_Pi_3/4.GPIO15
  N51: Green4.Pin_0, Raspberry_Pi_3/4.GPIO12
  N52: Green2.Pin_0, Raspberry_Pi_3/4.GPIO10
  N53: Green5.Pin_0, Raspberry_Pi_3/4.GPIO13
  N54: Green6.Pin_0, Raspberry_Pi_3/4.GPIO14
  N55: Green3.Pin_0, Raspberry_Pi_3/4.GPIO11
  N56: Raspberry_Pi_3/4.3v3, J16.pin4
  N57: Raspberry_Pi_3/4.GPIO2, J13.pin2, J16.pin2
  N58: Raspberry_Pi_3/4.GPIO3, J14.pin2, J16.pin1
  N59: Raspberry_Pi_3/4.GPIO27, J16.pin6
  N60: Raspberry_Pi_3/4.GPIO22, J4.pin1
  N61: Raspberry_Pi_3/4.GPIO26, J16.pin5
  N62: Raspberry_Pi_3/4.GPIO23, J5.pin1
  N63: Raspberry_Pi_3/4.5V, J3.pin1, J11.pin1, J12.pin1, J15.pin4
  N64: TRS1.Sleeve, RIn_G_LIn1.pin2, Volume.pin_3, Volume.pin_6, J6.pin2
  N65: TRS1.Ring, Volume.pin_1, Audio_R.pad
  N66: TRS1.Tip, Volume.pin_4, Audio_L.pad
  N67: L-_L+1.pin1, L+_L-.pin_2
  N68: L-_L+1.pin2, L+_L-.pin_1
  N69: RIn_G_LIn1.pin1, Volume.pin_2, J6.pin3
  N70: RIn_G_LIn1.pin3, Volume.pin_5, J6.pin1
  N71: J24.pin1, J25.pin1, 74F04.connector3, 74F04.connector9
  N72: J26.pin2, Logic_Conv.HV
  N73: J26.pin3, Arduino_Pro_Micro.D7
  N74: J26.pin4, Logic_Conv.TX_HV
  GND: J26.pin5, Arduino_Pro_Micro.GND, Logic_Conv.GND, 74F04.connector6
  N75: Arduino_Pro_Micro.D2, Logic_Conv.TX2_HV
  N76: Arduino_Pro_Micro.D3, Logic_Conv.RX2_HV
  N77: Logic_Conv.TX2_LV, 74F04.connector12
  N78: Logic_Conv.RX2_LV, 74F04.connector0
  N79: Logic_Conv.LV, 74F04.connector13
  N80: 74F04.connector1, 74F04.connector2
  N81: 74F04.connector10, 74F04.connector11

notes:
  PAM8610
  P1 Btn4
  P1 Btn5
  P1 Btn6
  P2 Btn4
  P2 Btn5
  P2 Btn6
  +5v
  GND
  Fan
  Vs Hs
  gnd
  CSync
  27 26
  +5v Gnd
  +3.3 Gnd
  Photo
  Trigger
  Gnd
  lightGun Module
  "PiPico Jamma", a Raspberry Pi based arcade board.
  License: GPLv3
  Antonio Tornisiello
  (a.k.a) Nino MegaDriver
  nino@nino.com.br

custom parts:
  Jamma Finger: PCB edge footprint for connecting Jamma dual 28pin connector - Updated by Nino MegaDriver
  Raspberry Pi 4: The RPi4, a faster version of the awesome Raspberry Pi 2 B ARM Board with 40 pin gpio. Ready for special Raspberry Pi B+ and RPi2 Hat (Hardware attached (on) top)
  Raspberry Pi Pico: Raspberry Pi Pico. Based around the RP2040 microcontroller the Pico is a low cost microcontroller device bringing Raspberry Pi quality, cost, and easy of use to the microcontroller space. Jan 2021, Split part in to two versions: tht (this one) and SMD. This one will drill holes for a .1 in header in pcb to allow plugging in the module as well as providing pads to solder the module to the top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
  Stereo POT: Stereo potentiometer
  Terminal 2pin: 2-pin Terminal Block
  74LS04: Hex Inverter
  74LS04: Hex Inverter
  74LS04: Hex Inverter
  74LS04: Hex Inverter
  74LS04: Hex Inverter
  74LS04: Hex Inverter
  74LS04: Hex Inverter
  74LS04: Hex Inverter
